# Fritzing sketch Arduino Trafik Işığı Modeli (saved by Fritzing 0.9.9b)
breadboards: 1

parts:
  Parça1 = Arduino Uno (Rev3)
  LED1 = LED - 5mm [color="Red (633nm)" current=0.030 package="5 mm [THT]"]
  R1 = Resistor [tolerance=±5% power=0.25 resistance=220 package=THT]
  LED2 = LED - 5mm [color="Green (555nm)" current=0.030 package="5 mm [THT]"]
  R2 = Resistor [tolerance=±5% power=0.25 resistance=220 package=THT]

nets:
  N1: Parça1.D8, LED1.anode
  N2: Parça1.GND, R1.Pin_0, R2.Pin_0
  N3: Parça1.D7, LED2.anode
  N4: LED1.cathode, R1.Pin_1
  N5: LED2.cathode, R2.Pin_1
